# Fritzing sketch LED (saved by Fritzing 0.9.2b)
breadboards: 1

parts:
  Componente1 = Arduino Mega 2560 (Rev3)
  LED1 = LED - 5mm [color="Blue (525nm)" package="5 mm [THT]"]
  R1 = Resistor [tolerance=±5% resistance=330 package=THT]

nets:
  N1: Componente1.GND, R1.Pin_0
  N2: Componente1.D11_PWM, LED1.anode
  N3: LED1.cathode, R1.Pin_1

notes:
  BLINK

// code stored in the sketch: Blink.ino
/*
  Blink
  
  Switching a LED on and off
  
  This example is part of the Fritzing Creator Kit: www.fritzing.org/creator-kit.
*/

int led = 11;                   // integer variable led is declared

void setup() {                  // the setup() method is executed only once
  pinMode(led, OUTPUT);         // the led PIN is declared as digital output
}

void loop() {                   // the loop() method is repeated
  digitalWrite(led, HIGH);      // switching on the led 
  delay(1000);                  // stopping the program for 1000 milliseconds
  digitalWrite(led, LOW);       // switching off the led 
  delay(1000);                  // stopping the program for 1000 milliseconds
}

// code stored in the sketch: Led.t.ino
#define LED 11  // Define o LED com o valor "11" que é onde o pino está conectado
                        
void setup() // Função setup é executada apenas uma vez
{
  pinMode (LED, OUTPUT); // Configura o pino do LED como saída
}

void loop() // Função loop é para executar repetidamente o código.
{
 digitalWrite(LED, HIGH);  // Acender LED
 delay(1000); // Aguarda 1000 milissegundos
 digitalWrite(LED,LOW); // Apagar LED
 delay(1000); // Aguarda 1000 milissegundos
 
}
